# Fritzing sketch SignalConditioner (saved by Fritzing 0.9.3b)
circuit board: 9.54845cm x 5.35cm
breadboards: 1

parts:
  U2 = LM 358 Dual Op-Amp [package="DIP8 [THT]"]
  U3 = LM 358 Dual Op-Amp [package="DIP8 [THT]"]
  R1 = Resistor [tolerance=±5% resistance=10k package=THT]
  R2 = Resistor [tolerance=±5% resistance=10k package=THT]
  D1 = Rectifier Diode [part_number=1N4148 package="300 mil [THT]"]
  D2 = Rectifier Diode [part_number=1N4148 package="300 mil [THT]"]
  R3 = Resistor [tolerance=±5% resistance=18k package=THT]
  R4 = Resistor [tolerance=±5% resistance=220k package=THT]
  J1 = female pin header, 2 pins [form="♀ (female)"]
  J2 = female pin header, 2 pins [form="♀ (female)"]
  U4 = LM 358 Dual Op-Amp [package="DIP8 [THT]"]
  R5 = Resistor [tolerance=±5% resistance=22k package=THT]
  R6 = Resistor [tolerance=±5% resistance=22k package=THT]
  R7 = Resistor [tolerance=±5% resistance=22k package=THT]
  R8 = Resistor [tolerance=±5% resistance=22k package=THT]
  J3 = female pin header, 2 pins [form="♀ (female)"]
  D3 = Rectifier Diode [part_number=1N4148 package="300 mil [THT]"]
  D4 = Rectifier Diode [part_number=1N4148 package="300 mil [THT]"]
  J4 = female pin header, 2 pins [form="♀ (female)"]
  R9 = Resistor [tolerance=±5% resistance=18k package=THT]
  R10 = Resistor [tolerance=±5% resistance=1.8k package=THT]
  R11 = Resistor [tolerance=±5% resistance=180 package=THT]
  D5 = Rectifier Diode [part_number=1N4001 package="300 mil [THT]"]
  D6 = Rectifier Diode [part_number=1N4001 package="300 mil [THT]"]
  D7 = Rectifier Diode [part_number=1N4001 package="300 mil [THT]"]
  D8 = Rectifier Diode [part_number=1N4001 package="300 mil [THT]"]
  C11 = Electrolytic Capacitor [capacitance=4.7mF voltage=16V package="300 mil [THT, electrolytic]"]
  C2 = Ceramic Capacitor [capacitance=10nF package="200 mil [THT, multilayer]"]
  C9 = Ceramic Capacitor [capacitance=1µF package="200 mil [THT, multilayer]"]
  C8 = Ceramic Capacitor [capacitance=100nF package="200 mil [THT, multilayer]"]
  C10 = Ceramic Capacitor [capacitance=100nF package="200 mil [THT, multilayer]"]
  J6 = female pin header, 2 pins [form="♀ (female)"]
  R16 = Resistor [tolerance=±5% resistance=0 package=THT]
  C1 = Ceramic Capacitor [capacitance=100nF package="200 mil [THT, multilayer]"]
  C13 = Ceramic Capacitor [capacitance=220nF package="200 mil [THT, multilayer]"]
  J7 = female pin header, 2 pins [form="♀ (female)"]
  J8 = female pin header, 2 pins [form="♀ (female)"]
  J9 = female pin header, 4 pins [form="♀ (female)"]
  IC1 = IC, DIP package, 8 pins [chip_label=IC]
  C14 = Ceramic Capacitor [capacitance=100nF package="200 mil [THT, multilayer]"]
  IC2 = IC, DIP package, 8 pins [chip_label=IC]
  J10 = female pin header, 4 pins [form="♀ (female)"]
  C15 = Ceramic Capacitor [capacitance=100nF package="200 mil [THT, multilayer]"]
  J11 = female pin header, 4 pins [form="♀ (female)"]
  C16 = Tantalum Capacitor [capacitance=2.2µF package="100 mil [THT, tantalum]"]
  R17 = Resistor [tolerance=±5% resistance=1k package=THT]
  J12 = female pin header, 1 pin [form="♀ (female)"]
  C17 = Tantalum Capacitor [capacitance=22µF package="200 mil [THT, tantalum]"]
  C5 = Ceramic Capacitor [capacitance=4.7nF package="100 mil [THT, multilayer]"]
  C4 = Ceramic Capacitor [capacitance=10nF package="100 mil [THT, multilayer]"]
  C6 = Ceramic Capacitor [capacitance=10nF package="100 mil [THT, multilayer]"]
  C7 = Ceramic Capacitor [capacitance=10nF package="100 mil [THT, multilayer]"]
  C12 = Ceramic Capacitor [capacitance=4.7nF package="100 mil [THT, multilayer]"]

nets:
  N1: U2.connector0, U2.connector1, U2.connector4, U3.connector2, D1.cathode, D2.anode, J2.pin2, D3.cathode, D4.anode, J4.pin1
  N2: U2.connector2, U3.connector4, R1.Pin_0, R2.Pin_1, C10.1, C17.+
  0V: U2.connector3, U3.connector3, R2.Pin_0, J1.pin2, U4.connector3, J3.pin2, C10.0, C1.0, J8.pin2, IC1.pin4, C14.0, IC2.pin4, C15.0, C16.-, C17.-, C5.0, C12.0
  N3: U2.connector5, D3.anode, D4.cathode, J4.pin2, R9.Pin_0, R10.Pin_0, R11.Pin_0, C9.0, C8.0, R17.Pin_1, C7.0
  N4: U2.connector6, IC1.pin2, J11.pin4
  3.3V: U2.connector7, U3.connector7, R1.Pin_1, U4.connector7, C1.1, J8.pin1, IC1.pin8, C14.1, IC2.pin8, C15.1, C16.+
  N5: U3.connector0, R3.Pin_1, R5.Pin_0, C2.1
  N6: U3.connector1, D1.anode, D2.cathode, R3.Pin_0, R4.Pin_1, C2.0
  N7: U3.connector5, U3.connector6, IC1.pin3, IC2.pin3
  N8: R4.Pin_0, J2.pin1
  N9: J1.pin1, U4.connector0, U4.connector1, C4.1
  N10: U4.connector2, R6.Pin_1, C12.1
  N11: U4.connector4, U4.connector6, J3.pin1, C6.1
  N12: U4.connector5, R7.Pin_1, C5.1
  N13: R5.Pin_1, R6.Pin_0, C4.0
  N14: R7.Pin_0, R8.Pin_1, C6.0
  N15: R8.Pin_0, IC2.pin1
  N16: R9.Pin_1, J11.pin3, C7.1
  N17: R10.Pin_1, C8.1, J11.pin2
  N18: R11.Pin_1, C9.1, J11.pin1
  N19: D5.cathode, D7.cathode, C11.+, C13.1, J9.pin3, J9.pin4
  N20: D5.anode, D6.cathode, J6.pin2
  N21: D6.anode, D8.anode, C11.-, C13.0, J7.pin2, J9.pin2
  N22: D7.anode, D8.cathode, R16.Pin_1
  N23: J6.pin1, R16.Pin_0
  N24: J7.pin1, J9.pin1
  N25: IC1.pin1, IC2.pin2
  N26: IC1.pin5, J10.pin4
  N27: IC1.pin6, IC2.pin6, J10.pin2
  N28: IC1.pin7, IC2.pin7, J10.pin1
  N29: IC2.pin5, J10.pin3
  N30: R17.Pin_0, J12.pin1

notes:
  6Vrms
  Vadc
  Iadc
  6.5ma RMS
  13A
  1.3A
  130mA
  1.65V
  6VRMS
  5Vout
  Gnd
  3.3Vin
  Pololu S7V8F5
  Vo
  Vi
  Shdn
  6VAC
  0V
  5V
  3V3
  Sck
  Sda
  CS1
  CS0 (labelled CS2 on PCB)
  Vref
  Iin
  Vin
  CS2
  TP1
  Signal conditioner
  TLV2472CP
  MCP6S91
  1.8Vpp measured
  Programmable gain amp. Gains with J11 1-4 linked.
  Gain = 100 Tested with 100ohm fed from transformer 220mApp (77.8mArms).
  77.8*230V = 17.9W. This gave 1.99Vpp. Full scale = 17.9*3.3/1.99 = 30W
  Gain = 10 -> 300W
  Gain = 1 -> 3KW
  C7, C8, R9, R10: DNF. Provided for physical gain selection switch in case PGA proved problematic. This was not the case.
  Op amp inputs transposed :-(
  CT impedance 240 ohms.
  7.8Vrms measured = 22Vpp
  Link 1-4.
  DNF: C7, C8, R9, R10.
